# Fritzing sketch Schema-Resistor-led (saved by Fritzing 0.9.3b)
breadboards: 1

parts:
  Onderdeel1 = Arduino Uno (Rev3)
  LED1 = LED - 5mm [color="Red (633nm)" package="5 mm [THT]"]
  R1 = Resistor [tolerance=±5% resistance=220 package=THT]
  R2 = Photocell (LDR) [package=THT]
  R3 = Resistor [tolerance=±5% resistance=220 package=THT]

nets:
  N1: Onderdeel1.A0, R2.pin_0, R3.Pin_1
  N2: Onderdeel1.D8, R1.Pin_0
  N3: Onderdeel1.5V, R2.pin_1
  N4: Onderdeel1.GND, LED1.cathode, R3.Pin_0
  N5: LED1.anode, R1.Pin_1
