# Fritzing sketch Schema-Photoresistor-buzzer (saved by Fritzing 0.9.3b)
breadboards: 1

parts:
  Onderdeel1 = Arduino Uno (Rev3)
  R2 = Photocell (LDR) [package=THT]
  R3 = Resistor [tolerance=±5% resistance=220 package=THT]
  SPKR1 = Loudspeaker
  R5 = Photocell (LDR) [package=THT]
  R6 = Photocell (LDR) [package=THT]
  R7 = Photocell (LDR) [package=THT]
  R8 = Resistor [tolerance=±5% resistance=220 package=THT]
  R9 = Resistor [tolerance=±5% resistance=220 package=THT]
  R10 = Resistor [tolerance=±5% resistance=220 package=THT]
  LED1 = LED - 5mm [color="Red (633nm)" package="5 mm [THT]"]
  R11 = Resistor [tolerance=±5% resistance=220 package=THT]

nets:
  N1: Onderdeel1.A0, R2.pin_0, R3.Pin_1
  N2: Onderdeel1.A1, R5.pin_0, R8.Pin_1
  N3: Onderdeel1.A2, R6.pin_0, R9.Pin_1
  N4: Onderdeel1.A3, R7.pin_0, R10.Pin_1
  N5: Onderdeel1.D8, SPKR1.pin2
  N6: Onderdeel1.5V, R2.pin_1, R5.pin_1, R6.pin_1, R7.pin_1, R11.Pin_1
  N7: Onderdeel1.GND, R3.Pin_0, SPKR1.pin1, R8.Pin_0, R9.Pin_0, R10.Pin_0, LED1.cathode
  N8: LED1.anode, R11.Pin_0
